# Fritzing sketch Beam Me Up (PCB) (saved by Fritzing 0.8.3b)
circuit board: 5.33115cm x 4.31518cm

parts:
  R3 = Resistor [tolerance=±5% resistance=10k package=THT]
  ATMEGA = atmega328 [package=dip]
  M1 = DC Motor
  R5 = Resistor [tolerance=±5% resistance=10k package=THT]
  M4 = DC Motor
  Y1 = Resonator [frequency="16 Mhz" package=THT]
  Q3 = NPN-Transistor [package="TO92 [THT]"]
  R2 = Resistor [tolerance=±5% resistance=10k package=THT]
  M2 = DC Motor
  R4 = Resistor [tolerance=±5% resistance=10k package=THT]
  Q1 = NPN-Transistor [package="TO92 [THT]"]
  Q4 = NPN-Transistor [package="TO92 [THT]"]
  R1 = Resistor [tolerance=±5% resistance=10k package=THT]
  C1 = Electrolytic Capacitor [capacitance=10µF package="100 mil [THT, electrolytic]"]
  M3 = DC Motor
  Q2 = NPN-Transistor [package="TO92 [THT]"]
  J1 = female pin header, 2 pins [form="♀ (female)"]
  3_7V = Battery

nets:
  N1: R3.Pin_0, ATMEGA.D9_(PWM)
  N2: R3.Pin_1, Q3.B
  N3: ATMEGA.RESET, R5.Pin_1
  N4: ATMEGA.D3_(PWM), R1.Pin_1
  N5: ATMEGA.VCC, M1.pin_2, R5.Pin_0, M2.pin_2, J1.pin1
  GND: ATMEGA.GND, Y1.GND, Q3.E, Q1.E, Q4.E, C1.-, Q2.E, 3_7V.-
  N6: ATMEGA.XLAT1, Y1.0
  N7: ATMEGA.XLAT2, Y1.pin_1
  N8: ATMEGA.D6_(PWM), R4.Pin_1
  N9: ATMEGA.D10_(PWM), R2.Pin_0
  N10: ATMEGA.AVCC, ATMEGA.AREF, M4.pin_2, M3.pin_2, J1.pin2
  N11: M1.pin_1, Q1.C
  N12: M4.pin_1, Q4.C
  N13: Q3.C, M3.pin_1
  N14: R2.Pin_1, Q2.B
  N15: M2.pin_1, Q2.C
  N16: R4.Pin_0, Q4.B
  N17: Q1.B, R1.Pin_0
  N18: C1.+, 3_7V.+

notes:
  +
  -
